# Fritzing sketch Circuit Layout (saved by Fritzing 0.9.8b)

parts:
  Part1 = Arduino Mega 2560 (Rev3)
  R1 = Slide Potentiometer [maximum_resistance=100kΩ]
  R2 = Slide Potentiometer [maximum_resistance=100kΩ]

nets:
  N1: Part1.A0, R1.wiper
  N2: Part1.A1, R2.wiper
  N3: Part1.5V, R1.leg2, R2.leg2
  N4: Part1.GND, R1.leg1, R2.leg1
